# Fritzing sketch launcher_valve_schematic (saved by Fritzing 0.8.6b)
breadboards: 1

parts:
  NPN = NPN-Transistor [package="TO92 [THT]"]
  part = Resistor [tolerance=±5% resistance=10k package=THT]
  Pull_Down = Resistor [tolerance=±5% resistance=10k package=THT]
  Pull_Up = Resistor [tolerance=±5% resistance=10k package=THT]
  P_MOSFET = Basic FET P-Channel [package="TO220 [THT]"]
  LOAD = Inductor [package="400 mil [THT]"]
  part_2 = Rectifier Diode [part_number=Diode package="300 mil [THT]"]

nets:
  N1: NPN.E, Pull_Up.Pin_1, P_MOSFET.gate
  N2: NPN.B, part.Pin_1, Pull_Down.Pin_0
  Arduino GND/GND: NPN.C, Pull_Down.Pin_1, LOAD.pin_1, part_2.cathode
  Arduino IO: part.Pin_0
  15V: Pull_Up.Pin_0, P_MOSFET.source
  N3: P_MOSFET.drain, LOAD.pin_0, part_2.anode
