# Fritzing sketch noderocket-launcher_electronics (saved by Fritzing 0.8.6b)
breadboards: 1

parts:
  Part1 = Arduino Uno (Rev3)
  R2 = Resistor [tolerance=±5% resistance=10k package=THT]
  R3 = Resistor [tolerance=±5% resistance=10k package=THT]
  Q2 = Basic FET P-Channel [package="TO220 [THT]"]
  L1 = Solenoid
  Q3 = NPN-Transistor [package="TO92 [THT]"]
  R4 = Resistor [tolerance=±5% resistance=10k package=THT]
  R5 = Resistor [tolerance=±5% resistance=10k package=THT]
  R6 = Resistor [tolerance=±5% resistance=10k package=THT]
  L2 = Solenoid
  Q4 = Basic FET P-Channel [package="TO220 [THT]"]
  D2 = Rectifier Diode [part_number=1N4148 package="Melf DO-213 AB [SMD]"]
  D1 = Rectifier Diode [part_number=1N4148 package="Melf DO-213 AB [SMD]"]
  R7 = Resistor [tolerance=±5% resistance=270 package=THT]
  U1 = mystery part, 2 pins [chip_label="pressure sensor"]
  Q1 = NPN-Transistor [package="TO92 [THT]"]
  R1 = Resistor [tolerance=±5% resistance=10k package=THT]
  JACK1 = 2.1mm DC Barrel Jack

nets (from the breadboard view):
  N1: Part1.A0, R7.Pin_1, U1.pin2
  N2: Part1.GND, L1.pin1, Q3.C, R4.Pin_0, L2.pin1, D2.anode, D1.anode, U1.pin1, Q1.C, R1.Pin_0, JACK1.switch
  N3: Part1.D2, R2.Pin_0
  N4: Part1.D3_PWM, R5.Pin_0
  N5: Part1.5V, R7.Pin_0
  N6: R2.Pin_1, Q1.B, R1.Pin_1
  N7: R3.Pin_0, Q2.gate, Q1.E
  N8: R3.Pin_1, Q2.source, R6.Pin_1, Q4.source, JACK1.center
  N9: Q2.drain, L1.pin2, D1.cathode
  N10: Q3.E, R6.Pin_0, Q4.gate
  N11: Q3.B, R4.Pin_1, R5.Pin_1
  N12: L2.pin2, Q4.drain, D2.cathode

notes:
  There are essentially 3 circuits here:
  1) A two transistor switch to control high current to an air valve.
  2) A second identical two transistor switch to control high current to a second air valve.
  3) A simple voltage divider to measure the resistance coming from an automobile oil pressure sensor
  This solenoid is an air valve to control the release of the rocket.
  This solenoid is an air valve to control the flow of pressurized air into the rocket and launcher.
  This generic part is an automobile oil pressure sensor - used to measure the air pressure in the rocket and launcher
  There are two sources of power in this circuit: 1) the +5V from the Arduino and 2) a +15V external source. The ground between the two sources are tied together. The +5 powers the pressure sensor and the NPN transistors. The +15V powers the P-channel MOSFETs and the solenoids.

custom parts:
  2.1mm DC Barrel Jack: 2.1mm DC Barrel Jack with Thru-Hole Connectors (breadboardable)
